// Logisim project cours01.circ as structural Verilog: 7 circuits, main circuit main
module main (
  input  [2:0] in_1,
  input  [2:0] in_2,
  input  in_3,
  input  in_4,
  input  in_5,
  output out_6,
  output out_7
);

  wire and_1_out, and_2_out, and_3_out, full_adder_3bits_1_p1;

  // full_adder_3bits full_adder_3bits_1: pin names not known; wires that end beside it: full_adder_3bits_1_p1
  xor xor_1 (out_6, in_3, in_4, in_5);
  and and_1 (and_1_out, ~in_3, in_5);  // AND_Gate
  and and_2 (and_2_out, ~in_3, in_4);  // AND_Gate
  and and_3 (and_3_out, in_5, in_5);
  or or_1 (out_7, and_1_out, and_2_out, and_3_out);
endmodule

module half_adder (
  input  in_1,
  input  in_2,
  output out_3,
  output out_4
);

  xor xor_1 (out_3, in_1, in_2);
  and and_1 (out_4, in_1, in_2);

  // Notes on the sheet:
  //   3ns
  //   2ns
endmodule

module full_adder_3bits (
  input  in_1,
  input  in_2,
  input  in_3,
  output out_4,
  output out_5
);

  wire and_1_out, and_2_out, and_3_out;

  xor xor_1 (out_4, in_1, in_3, in_2);
  and and_1 (and_1_out, in_1, in_2);
  and and_2 (and_2_out, in_1, in_3);
  and and_3 (and_3_out, in_2, in_3);
  or or_1 (out_5, and_1_out, and_2_out, and_3_out);
endmodule

module full_adder_3bits_serie (
  input  in_1,
  input  in_2,
  input  in_3,
  output out_4,
  output _7ns
);

  wire half_adder_1_out_3, half_adder_1_out_4, half_adder_2_out_4;

  half_adder half_adder_1 (.in_1(in_3), .in_2(in_2), .out_3(half_adder_1_out_3), .out_4(half_adder_1_out_4));
  half_adder half_adder_2 (.in_1(in_1), .in_2(half_adder_1_out_3), .out_3(out_4), .out_4(half_adder_2_out_4));
  or or_1 (_7ns, half_adder_2_out_4, half_adder_1_out_4);

  // Notes on the sheet:
  //   3ns
  //   2ns
  //   3ns
  //   2ns
  //   2ns
  //   2ns
  //   6ns
endmodule

module ripple_carry (
  input  in_1,
  input  in_2,
  input  in_3,
  input  in_4,
  input  in_5,
  input  in_6,
  input  in_7,
  input  in_8,
  input  in_9,
  output plus_4ns,
  output out_11,
  output out_12,
  output out_13,
  output out_14
);

  wire full_adder_3bits_2_out_5, full_adder_3bits_3_out_5, full_adder_3bits_4_out_5;

  full_adder_3bits full_adder_3bits_1 (
    .in_1(in_5), .in_2(in_1), .in_3(full_adder_3bits_2_out_5), .out_4(out_11), .out_5(plus_4ns));
  full_adder_3bits full_adder_3bits_2 (
    .in_1(in_6), .in_2(in_2), .in_3(full_adder_3bits_3_out_5), .out_4(out_12),
    .out_5(full_adder_3bits_2_out_5));
  full_adder_3bits full_adder_3bits_3 (
    .in_1(in_7), .in_2(in_3), .in_3(full_adder_3bits_4_out_5), .out_4(out_13),
    .out_5(full_adder_3bits_3_out_5));
  full_adder_3bits full_adder_3bits_4 (
    .in_1(in_8), .in_2(in_4), .in_3(in_9), .out_4(out_14), .out_5(full_adder_3bits_4_out_5));

  // Notes on the sheet:
  //   +4ns
  //   +4ns
  //   +7ns
  //   full-adder worst-case: 7ns + 4ns * 3 = 19ns
  //   full-adder worst-case: 19ns + 4ns * 4 = 35ns
  //   half-adder worst-case: max(XOR, AND) : 3ns
endmodule

module addsub (
  input  in_1,
  input  in_2,
  input  in_3,
  input  in_4,
  input  in_5,
  input  in_6,
  input  in_7,
  input  in_8,
  input  in_9,
  input  X,
  input  Y,
  input  S,
  output out_13,
  output out_14,
  output out_15,
  output out_16,
  output out_17,
  output out_18,
  output out_19
);

  wire full_adder_3bits_2_out_5, full_adder_3bits_4_out_5, full_adder_3bits_5_out_5, not_1_out, not_2_out,
       xor_1_out, xor_2_out, xor_3_out, xor_4_out, xor_5_out;

  xor xor_1 (xor_1_out, in_5, in_9);
  full_adder_3bits full_adder_3bits_1 (
    .in_1(xor_1_out), .in_2(in_1), .in_3(full_adder_3bits_2_out_5), .out_4(out_14), .out_5(out_13));
  full_adder_3bits full_adder_3bits_2 (
    .in_1(xor_2_out), .in_2(in_2), .in_3(full_adder_3bits_4_out_5), .out_4(out_15),
    .out_5(full_adder_3bits_2_out_5));
  full_adder_3bits full_adder_3bits_3 (.in_1(xor_3_out), .in_2(X), .in_3(not_2_out), .out_4(out_19), .out_5(out_18));
  xor xor_2 (xor_2_out, in_6, in_9);
  xor xor_3 (xor_3_out, Y, not_1_out);
  not not_1 (not_1_out, not_2_out);
  not not_2 (not_2_out, S);
  xor xor_4 (xor_4_out, in_7, in_9);
  full_adder_3bits full_adder_3bits_4 (
    .in_1(xor_4_out), .in_2(in_3), .in_3(full_adder_3bits_5_out_5), .out_4(out_16),
    .out_5(full_adder_3bits_4_out_5));
  full_adder_3bits full_adder_3bits_5 (
    .in_1(xor_5_out), .in_2(in_4), .in_3(in_9), .out_4(out_17), .out_5(full_adder_3bits_5_out_5));
  xor xor_5 (xor_5_out, in_8, in_9);
endmodule

module transistors (
  input  in_1,
  input  in_2,
  input  in_3
);

  wire transistor_1_out, transistor_3_out, transistor_4_out, transistor_5_out;

  Transistor transistor_1 (.in(1'b1), .out(transistor_1_out), .gate(in_1));
  Transistor #(.\type ("n")) transistor_2 (.in(1'b0), .out(transistor_1_out), .gate(in_1));
  LED led_1 (.in(transistor_1_out));
  Transistor transistor_3 (.in(1'b1), .out(transistor_3_out), .gate(in_2));
  Transistor transistor_4 (.in(transistor_3_out), .out(transistor_4_out), .gate(in_3));
  Transistor #(.\type ("n")) transistor_5 (.in(transistor_4_out), .out(transistor_5_out), .gate(in_2));
  Transistor #(.\type ("n")) transistor_6 (.in(transistor_4_out), .out(transistor_5_out), .gate(in_3));
  LED led_2 (.in(transistor_4_out));
  // also tied to GND on the sheet: transistor_5_out
endmodule
