// Logisim project serie01.circ as structural Verilog: 1 circuit, main circuit main
module main (
  input  in_1,
  input  in_2,
  input  in_3,
  input  a,
  input  b,
  input  c,
  input  in_7,
  input  in_8,
  input  in_9,
  input  in_10,
  input  in_11,
  input  in_12,
  input  in_13,
  input  in_14,
  input  in_15,
  input  in_16,
  input  in_17
);

  wire a_b_c_out, a_c_out, a_nb_nc_out, a_or_b_and_c_out, and_1_out, and_2_out, and_3_out, and_4_out,
       and_5_out, and_6_out, and_7_out, and_8_out, c_not_b_out, na_b_nc_out, na_nb_c_out, not_1_out,
       not_2_out, not_3_out, not_4_out, not_5_out, not_6_out, not_7_out, not_8_out, not_9_out, not_10_out,
       not_11_out, not_12_out, not_13_out, not_14_out, not_15_out, not_16_out, not_17_out,
       not_a_and_b_not_c_out, not_a_b_not_c_out, or_1_out, or_2_out, or_3_out, or_5_out, or_6_out, or_7_out,
       or_8_out, or_9_out, or_10_out, xnor_1_out, xor_1_out, xor_2_out, xor_3_out;

  not not_1 (not_1_out, in_2);
  not not_2 (not_2_out, in_3);
  xor xor_1 (xor_1_out, in_1, not_1_out);
  xor xor_2 (xor_2_out, not_1_out, not_2_out);
  not not_3 (not_3_out, b);
  not not_4 (not_4_out, c);
  not not_5 (not_5_out, a);
  not not_6 (not_6_out, c);
  not not_7 (not_7_out, a);
  not not_8 (not_8_out, b);
  not not_9 (not_9_out, in_7);
  not not_10 (not_10_out, in_9);
  not not_11 (not_11_out, in_15);
  not not_12 (not_12_out, in_13);
  and and_1 (and_1_out, in_3, xor_1_out);
  xor xor_3 (xor_3_out, not_2_out, in_1);
  and and_2 (and_2_out, not_9_out, in_9);
  and and_3 (and_3_out, not_10_out, in_11);
  or or_1 (or_1_out, in_13, not_11_out);
  or or_2 (or_2_out, not_12_out, in_15);
  xnor xnor_1 (xnor_1_out, in_13, in_15);
  or or_3 (or_3_out, and_1_out, and_4_out);
  and and_4 (and_4_out, in_1, xor_2_out);
  and a_b_c (a_b_c_out, a, b, c);
  and a_nb_nc (a_nb_nc_out, a, not_3_out, not_4_out);
  and na_b_nc (na_b_nc_out, not_5_out, b, not_6_out);
  and na_nb_c (na_nb_c_out, not_7_out, not_8_out, c);
  and and_5 (and_5_out, or_1_out, or_2_out);
  and and_6 (and_6_out, xor_3_out, in_2);
  // OR_Gate or_4 has open pins: in0=and_2_out, in1=and_3_out, out=open
  LED led_1 (.in(and_5_out));
  LED led_2 (.in(xnor_1_out));
  or or_5 (or_5_out, or_3_out, and_6_out);
  LED led_3 (.in(or_5_out));
  or or_6 (or_6_out, a_b_c_out, a_nb_nc_out, na_b_nc_out, na_nb_c_out);
  LED led_4 (.in(or_6_out));
  not not_13 (not_13_out, in_12);
  not not_14 (not_14_out, in_8);
  not not_15 (not_15_out, in_16);
  not not_16 (not_16_out, in_17);
  not not_17 (not_17_out, in_17);
  and and_7 (and_7_out, not_13_out, not_14_out);
  or or_7 (or_7_out, in_8, in_10);
  and a_c (a_c_out, in_17, in_14);
  and c_not_b (c_not_b_out, in_17, not_15_out);
  and and_8 (and_8_out, in_16, not_16_out);
  and a_or_b_and_c (a_or_b_and_c_out, or_7_out, in_12);
  and not_a_b_not_c (not_a_b_not_c_out, and_7_out, in_10);
  or or_8 (or_8_out, a_c_out, c_not_b_out);
  and not_a_and_b_not_c (not_a_and_b_not_c_out, and_8_out, not_17_out);
  or or_9 (or_9_out, or_8_out, not_a_and_b_not_c_out);
  or or_10 (or_10_out, not_a_b_not_c_out, a_or_b_and_c_out);
  LED led_5 (.in(or_9_out));
  LED led_6 (.in(or_10_out));
endmodule
