// Logisim project serie02.circ as structural Verilog: 1 circuit, main circuit main
module main (
  input  a,
  input  b,
  input  c,
  input  a_2,
  input  c_2,
  input  b_2,
  input  [2:0] in_7,
  input  in_8,
  input  in_9,
  input  in_10,
  input  in_11,
  input  in_12,
  input  in_13,
  input  in_14,
  input  in_15,
  input  in_16,
  input  in_17,
  input  in_18,
  input  in_19,
  input  in_20
);

  wire a_b_c_2_out, a_barre_b_out, a_barre_c_out, and_1_out, and_2_out, and_3_out, and_4_out, and_5_out,
       and_6_out, nand_1_out, nand_2_out, nand_3_out, nand_4_out, nand_5_out, nand_6_out, nand_7_out,
       nand_8_out, nand_9_out, nand_10_out, nand_11_out, nand_12_out, nand_13_out, nand_14_out, nand_15_out,
       nand_17_out, nand_18_out, nand_19_out, nand_20_out, nand_21_out, nand_22_out, nand_23_out,
       nand_24_out, nand_25_out, nor_1_out, nor_2_out, nor_3_out, nor_4_out, nor_5_out, nor_6_out, nor_7_out,
       nor_8_out, nor_9_out, not_1_out, not_2_out, not_3_out, not_4_out, or_1_out, or_2_out, or_3_out;

  not not_1 (not_1_out, a_2);
  not not_2 (not_2_out, a);
  nand nand_1 (nand_1_out, in_8, in_8);
  nand nand_2 (nand_2_out, in_9, in_9);
  nand nand_3 (nand_3_out, in_10, in_10);
  nand nand_4 (nand_4_out, in_11, in_11);
  nand nand_5 (nand_5_out, in_12, in_12);
  nand nand_6 (nand_6_out, in_13, in_13);
  nand nand_7 (nand_7_out, in_15, in_15);
  nand nand_8 (nand_8_out, in_17, in_17);
  nor nor_1 (nor_1_out, in_18, in_18);
  nor nor_2 (nor_2_out, in_19, in_19);
  nor nor_3 (nor_3_out, in_20, in_20);
  not not_3 (not_3_out, c);
  and a_barre_c (a_barre_c_out, not_1_out, c_2);
  and a_barre_b (a_barre_b_out, not_1_out, b_2);
  and a_b_c_2 (a_b_c_2_out, a_2, c_2);
  and and_1 (and_1_out, not_2_out, c);
  and and_2 (and_2_out, b, not_3_out);
  nand nand_9 (nand_9_out, in_14, in_15);
  nand nand_10 (nand_10_out, in_17, in_16);
  nand nand_11 (nand_11_out, in_14, nand_7_out);
  nand nand_12 (nand_12_out, in_14, in_17);
  nand nand_13 (nand_13_out, nand_7_out, nand_8_out);
  nand nand_14 (nand_14_out, nand_7_out, in_17);
  nand nand_15 (nand_15_out, nand_1_out, nand_2_out, in_10);
  nand nand_16 (nand_15_out, nand_1_out, in_9, nand_3_out);
  nand nand_17 (nand_17_out, nand_3_out, nand_2_out, in_8);
  nand nand_18 (nand_18_out, in_10, in_9, in_8);
  nor nor_4 (nor_4_out, nor_3_out, nor_2_out, in_18);
  nor nor_5 (nor_5_out, nor_1_out, in_20, in_19);
  nor nor_6 (nor_6_out, nor_1_out, nor_2_out, in_20);
  nor nor_7 (nor_7_out, nor_1_out, nor_2_out, nor_3_out);
  and and_3 (and_3_out, a, b);
  or or_1 (or_1_out, a_barre_c_out, a_barre_b_out, a_b_c_2_out);
  LED led_1 (.in(or_1_out));
  not not_4 (not_4_out, in_7[0]);
  nand nand_19 (nand_19_out, nand_4_out, nand_5_out, in_13);
  nand nand_20 (nand_20_out, nand_4_out, in_12, nand_6_out);
  nand nand_21 (nand_21_out, in_11, nand_5_out, nand_6_out);
  nand nand_22 (nand_22_out, in_11, in_12, in_13);
  or or_2 (or_2_out, and_3_out, and_1_out, and_2_out);
  LED led_2 (.in(or_2_out));
  and and_4 (and_4_out, not_4_out, in_7[2]);
  and and_5 (and_5_out, not_4_out, in_7[2]);
  and and_6 (and_6_out, in_7[0], in_7[2], in_7[2]);
  LED led_3 (.in(nand_23_out));
  nand nand_23 (nand_23_out, nand_15_out, nand_15_out, nand_17_out, nand_18_out);
  nand nand_24 (nand_24_out, nand_9_out, nand_10_out, nand_11_out, nand_12_out, nand_13_out, nand_14_out);
  LED led_4 (.in(nand_24_out));
  nor nor_8 (nor_8_out, nor_4_out, nor_5_out, nor_6_out, nor_7_out);
  nand nand_25 (nand_25_out, nand_19_out, nand_20_out, nand_21_out, nand_22_out);
  LED led_5 (.in(nand_25_out));
  nor nor_9 (nor_9_out, nor_8_out, nor_8_out);
  LED led_6 (.in(nor_9_out));
  or or_3 (or_3_out, and_4_out, and_5_out, and_6_out);
  LED led_7 (.in(or_3_out));

  assign in_7[1] = in_7[2];

  // Notes on the sheet:
  //   metoda de valerio
endmodule
