// Logisim project serie03.circ as structural Verilog: 2 circuits, main circuit main
module main (
  input  W,
  input  X,
  input  Y,
  input  Z,
  input  in_5,
  input  in_6,
  input  in_7,
  input  in_8,
  input  in_9
);

  wire a_out, and_1_out, and_2_out, and_3_out, and_4_out, and_5_out, and_6_out, and_7_out, and_8_out,
       and_9_out, and_10_out, and_11_out, and_12_out, and_13_out, and_14_out, and_15_out, and_16_out,
       and_17_out, and_18_out, and_19_out, and_20_out, and_21_out, and_22_out, and_23_out, and_24_out,
       and_25_out, and_26_out, and_27_out, and_28_out, and_29_out, and_30_out, and_31_out, and_32_out,
       and_33_out, and_34_out, b_out, c_out, clock_1_out, clock_2_out, clock_3_out, clock_4_out, clock_5_out,
       clock_6_out, clock_7_out, clock_8_out, d_out, e_out, f_out, g_out, h_1_out_5, not_1_out, not_2_out,
       not_3_out, not_4_out, not_5_out, not_6_out, not_7_out, not_8_out, not_9_out, not_10_out, not_11_out,
       not_12_out, not_13_out, not_14_out, not_15_out, not_16_out, or_1_out, or_2_out, or_3_out, or_4_out,
       or_5_out, or_6_out, or_7_out, xnor_1_out, xnor_2_out;

  Clock #(.highDuration(2), .lowDuration(2)) clock_1 (.out(clock_1_out));
  Clock clock_2 (.out(clock_2_out));
  Clock #(.highDuration(10), .lowDuration(10)) clock_3 (.out(clock_3_out));
  Clock #(.highDuration(4), .lowDuration(4)) clock_4 (.out(clock_4_out));
  Clock #(.highDuration(2), .lowDuration(2)) clock_5 (.out(clock_5_out));
  Clock clock_6 (.out(clock_6_out));
  Clock #(.lowDuration(10)) clock_7 (.out(clock_7_out));
  Clock #(.highDuration(4), .lowDuration(4)) clock_8 (.out(clock_8_out));
  not not_1 (not_1_out, clock_7_out);
  not not_2 (not_2_out, clock_8_out);
  not not_3 (not_3_out, clock_1_out);
  not not_4 (not_4_out, clock_2_out);
  not not_5 (not_5_out, clock_3_out);
  not not_6 (not_6_out, clock_4_out);
  not not_7 (not_7_out, clock_5_out);
  not not_8 (not_8_out, clock_6_out);
  not not_9 (not_9_out, not_1_out);
  not not_10 (not_10_out, not_2_out);
  not not_11 (not_11_out, not_3_out);
  not not_12 (not_12_out, not_4_out);
  not not_13 (not_13_out, not_5_out);
  not not_14 (not_14_out, not_6_out);
  not not_15 (not_15_out, not_7_out);
  not not_16 (not_16_out, not_8_out);
  h h_1 (.in_1(clock_3_out), .in_2(clock_4_out), .in_3(clock_5_out), .in_4(clock_6_out), .out_5(h_1_out_5));
  and and_1 (and_1_out, not_9_out, not_2_out, not_3_out);
  and and_2 (and_2_out, not_1_out, not_10_out, not_12_out);
  and and_3 (and_3_out, not_1_out, not_2_out, not_4_out);
  and and_4 (and_4_out, not_1_out, not_11_out);
  and and_5 (and_5_out, not_1_out, not_2_out);
  and and_6 (and_6_out, not_1_out, not_11_out, not_12_out);
  and and_7 (and_7_out, not_1_out, not_3_out, not_4_out);
  and and_8 (and_8_out, not_2_out, not_3_out);
  and and_9 (and_9_out, not_1_out, not_10_out);
  and and_10 (and_10_out, not_1_out, not_12_out);
  and and_11 (and_11_out, not_2_out, not_3_out);
  and and_12 (and_12_out, not_9_out, not_2_out, not_3_out);
  and and_13 (and_13_out, not_1_out, not_10_out, not_3_out, not_12_out);
  and and_14 (and_14_out, not_1_out, not_2_out, not_11_out);
  and and_15 (and_15_out, not_1_out, not_2_out, not_4_out);
  and and_16 (and_16_out, not_1_out, not_11_out, not_4_out);
  and and_17 (and_17_out, not_1_out, not_11_out, not_4_out);
  and and_18 (and_18_out, not_2_out, not_3_out, not_4_out);
  and and_19 (and_19_out, not_9_out, not_2_out, not_3_out);
  and and_20 (and_20_out, not_1_out, not_10_out, not_3_out);
  and and_21 (and_21_out, not_1_out, not_10_out, not_4_out);
  and and_22 (and_22_out, not_1_out, not_3_out, not_4_out);
  and and_23 (and_23_out, not_9_out, not_2_out, not_3_out);
  and and_24 (and_24_out, not_1_out, not_10_out, not_3_out);
  and and_25 (and_25_out, not_1_out, not_10_out, not_4_out);
  and and_26 (and_26_out, not_1_out, not_2_out, not_11_out);
  or a (a_out, and_1_out, and_2_out, and_3_out, and_4_out);
  or b (b_out, and_5_out, and_6_out, and_7_out, and_8_out);
  or c (c_out, and_9_out, and_10_out, and_11_out);
  or d (d_out, and_12_out, and_13_out, and_14_out, and_15_out, and_16_out);
  or e (e_out, and_17_out, and_18_out);
  or f (f_out, and_19_out, and_20_out, and_21_out, and_22_out);
  or g (g_out, and_23_out, and_24_out, and_25_out, and_26_out);
  xnor xnor_1 (xnor_1_out, not_6_out, not_8_out);
  xnor xnor_2 (xnor_2_out, not_15_out, not_16_out);
  and and_27 (and_27_out, not_14_out, not_7_out, not_16_out);
  and and_28 (and_28_out, not_6_out, not_8_out);
  and and_29 (and_29_out, not_6_out, not_15_out);
  and and_30 (and_30_out, not_15_out, not_8_out);
  and and_31 (and_31_out, not_15_out, not_8_out);
  and and_32 (and_32_out, not_6_out, not_8_out);
  and and_33 (and_33_out, not_7_out, not_8_out);
  and and_34 (and_34_out, not_6_out, not_15_out);
  or or_1 (or_1_out, xnor_1_out, not_15_out, not_13_out);
  or or_2 (or_2_out, xnor_2_out, not_6_out);
  or or_3 (or_3_out, not_14_out, not_7_out, not_16_out);
  or or_4 (or_4_out, and_27_out, and_28_out, and_29_out, and_30_out, not_13_out);
  or or_5 (or_5_out, and_31_out, and_32_out);
  or or_6 (or_6_out, and_33_out, h_1_out_5);
  or or_7 (or_7_out, and_34_out, h_1_out_5);
  _7_Segment_Display u_7_segment_display_1 (
    .g(g_out), .f(f_out), .a(a_out), .b(b_out), .e(e_out), .d(d_out), .c(c_out));  // open: dp
  _7_Segment_Display u_7_segment_display_2 (
    .g(or_7_out), .f(or_6_out), .a(or_1_out), .b(or_2_out), .e(or_5_out), .d(or_4_out), .c(or_3_out));  // open: dp
endmodule

module h (
  input  in_1,
  input  in_2,
  input  in_3,
  input  in_4,
  output out_5
);

  wire and_1_out, and_2_out;

  and and_1 (and_1_out, in_2, ~in_3);  // AND_Gate
  and and_2 (and_2_out, in_2, ~in_4);  // AND_Gate
  or or_1 (out_5, in_1, and_1_out, and_2_out);
endmodule
