// Logisim project lab02.circ as structural Verilog: 3 circuits, main circuit main
module main (
  input  A1,
  input  B1,
  input  C1,
  input  A2,
  input  B2,
  input  C2,
  input  D2
);

  wire equation_1_1_out_4, equation_2_1_out_5;

  LED led_1 (.in(equation_1_1_out_4));
  equation_1 equation_1_1 (.InA(A1), .InB(B1), .InC(C1), .out_4(equation_1_1_out_4));
  LED led_2 (.in(equation_2_1_out_5));
  equation_2 equation_2_1 (.InA(A2), .InB(B2), .InC(C2), .InD(D2), .out_5(equation_2_1_out_5));
endmodule

module equation_1 (
  input  InA,
  input  InB,
  input  InC,
  output out_4
);

  wire and_1_out, and_2_out, and_3_out;

  and and_1 (and_1_out, ~InA, InB, ~InC);  // AND_Gate
  and and_2 (and_2_out, InA, ~InB, ~InC);  // AND_Gate
  and and_3 (and_3_out, InA, InB, InC);
  or or_1 (out_4, and_1_out, and_2_out, and_3_out);
endmodule

module equation_2 (
  input  InA,
  input  InB,
  input  InC,
  input  InD,
  output out_5
);

  wire and_1_out, and_2_out, and_3_out, and_4_out;

  and and_1 (and_1_out, ~InA, ~InB, InC, ~InD);  // AND_Gate
  and and_2 (and_2_out, ~InA, InB, InC, InD);  // AND_Gate
  and and_3 (and_3_out, InA, ~InB, InC, ~InD);  // AND_Gate
  and and_4 (and_4_out, InA, InB, InC, ~InD);  // AND_Gate
  or or_1 (out_5, and_1_out, and_2_out, and_3_out, and_4_out);

  // Notes on the sheet:
  //   (A'B'CD')+(A'BCD)+(AB'CD')+(ABCD')
endmodule
