// Logisim project lab03.circ as structural Verilog: 2 circuits, main circuit main
module main (
  input  in_1,
  input  in_2,
  input  in_3,
  input  in_4,
  input  in_5,
  input  in_6,
  input  in_7,
  input  in_8,
  input  in_9
);

  wire [3:0] encoder_2_out_10;

  encoder encoder_1 ();  // open: In1, In2, In3, In4, In5, In6, In7, In8, In9, out_10, out_11, out_12, out_13
  encoder encoder_2 (
    .In1(in_1), .In2(in_2), .In3(in_3), .In4(in_4), .In5(in_5), .In6(in_6), .In7(in_7), .In8(in_8),
    .In9(in_9), .out_10(encoder_2_out_10[0]), .out_11(encoder_2_out_10[1]), .out_12(encoder_2_out_10[2]),
    .out_13(encoder_2_out_10[3]));
  Hex_Digit_Display hex_digit_display_1 (.value(encoder_2_out_10));  // open: dp
endmodule

module encoder (
  input  In1,
  input  In2,
  input  In3,
  input  In4,
  input  In5,
  input  In6,
  input  In7,
  input  In8,
  input  In9,
  output out_10,
  output out_11,
  output out_12,
  output out_13
);

  wire U1_out, U2_out, U3_out, U4_out, U5_out, U6_out, U7_out, U8_out, U9_out, U10_out, U11_out, U12_out,
       U16_out;

  nor U16 (U16_out, In8, In9);
  and U1 (U1_out, In1, ~In2, ~In4, ~In6, U16_out);  // AND_Gate
  and U2 (U2_out, In3, ~In4, ~In6, U16_out);  // AND_Gate
  and U3 (U3_out, In5, ~In6, U16_out);  // AND_Gate
  and U4 (U4_out, In7, U16_out);
  and U5 (U5_out, In2, ~In4, In5, ~U16_out);  // AND_Gate
  and U6 (U6_out, ~In4, ~In5, In3, U16_out);  // AND_Gate
  and U7 (U7_out, In6, U16_out);
  and U8 (U8_out, In7, U16_out);
  and U9 (U9_out, In4, U16_out);
  and U10 (U10_out, In5, U16_out);
  and U11 (U11_out, In6, U16_out);
  and U12 (U12_out, In7, U16_out);
  or U13 (out_10, U1_out, U2_out, U3_out, U4_out, In9);
  or U14 (out_11, U5_out, U6_out, U7_out, U8_out);
  or U15 (out_12, U9_out, U10_out, U11_out, U12_out);
  or U17 (out_13, In9, In8);
endmodule
